// Logisim project lab4_part1.circ as structural Verilog
module FullAdder_1bit (
  input  A,
  input  B,
  input  C_in,
  output S,
  output C_out
);

  wire and_1_out, and_2_out, xor_1_out;

  xor xor_1 (xor_1_out, A, B);
  xor xor_2 (S, xor_1_out, C_in);
  and and_1 (and_1_out, xor_1_out, C_in);
  and and_2 (and_2_out, B, A);
  or or_1 (C_out, and_1_out, and_2_out);
endmodule

module ALU_1bit (
  input  [3:0] ALU_Ctrl,
  input  A,
  input  B,
  input  C_in,
  output R,
  output C_out
);

  wire and_1_out, fulladder_1bit_1_s, multiplexer_1_out, not_1_out, or_1_out, xor_1_out;

  Multiplexer #(.enable("false")) multiplexer_1 (.in0(B), .in1(not_1_out), .out(multiplexer_1_out), .sel(ALU_Ctrl[2]));
  not not_1 (not_1_out, B);
  and and_1 (and_1_out, A, multiplexer_1_out);
  or or_1 (or_1_out, A, multiplexer_1_out);
  xor xor_1 (xor_1_out, A, multiplexer_1_out);
  FullAdder_1bit fulladder_1bit_1 (.A(A), .B(multiplexer_1_out), .C_in(C_in), .S(fulladder_1bit_1_s), .C_out(C_out));
  Multiplexer #(.enable("false"), .select(2)) multiplexer_2 (
    .in0(and_1_out), .in1(or_1_out), .in2(xor_1_out), .in3(fulladder_1bit_1_s), .out(R), .sel(ALU_Ctrl[1:0]));
endmodule

module ALU_Control (
  input  I30,
  input  I14,
  input  I13,
  input  I12,
  input  I6,
  input  I5,
  input  I4,
  output ALU_Ctrl3,
  output ALU_Ctrl2,
  output ALU_Ctrl1,
  output ALU_Ctrl0,
  output ALU_Src
);

  wire and_2_out, not_1_out, not_2_out, not_3_out, not_4_out, not_5_out;

  not not_1 (not_1_out, I14);
  not not_2 (not_2_out, I13);
  not not_3 (not_3_out, I12);
  not not_4 (not_4_out, I5);
  not not_5 (not_5_out, I4);
  and and_1 (ALU_Ctrl2, I30, not_2_out, I5);
  or or_1 (ALU_Ctrl1, not_2_out, not_5_out);
  and and_2 (and_2_out, I13, not_3_out);
  or or_2 (ALU_Src, not_4_out, not_5_out);
  or or_3 (ALU_Ctrl0, not_1_out, and_2_out);

  assign ALU_Ctrl3 = 1'b0;
endmodule

module ALU_4bit (
  input  [3:0] ALU_Ctrl,
  input  C_in,
  input  [3:0] A,
  input  [3:0] B,
  output [3:0] R,
  output C_out
);

  wire alu_1bit_1_c_out, alu_1bit_2_c_out, alu_1bit_3_c_out;

  ALU_1bit alu_1bit_1 (.ALU_Ctrl(ALU_Ctrl), .A(A[0]), .B(B[0]), .C_in(C_in), .R(R[0]), .C_out(alu_1bit_1_c_out));
  ALU_1bit alu_1bit_2 (
    .ALU_Ctrl(ALU_Ctrl), .A(A[1]), .B(B[1]), .C_in(alu_1bit_1_c_out), .R(R[1]), .C_out(alu_1bit_2_c_out));
  ALU_1bit alu_1bit_3 (
    .ALU_Ctrl(ALU_Ctrl), .A(A[2]), .B(B[2]), .C_in(alu_1bit_2_c_out), .R(R[2]), .C_out(alu_1bit_3_c_out));
  ALU_1bit alu_1bit_4 (.ALU_Ctrl(ALU_Ctrl), .A(A[3]), .B(B[3]), .C_in(alu_1bit_3_c_out), .R(R[3]), .C_out(C_out));
endmodule

module ALU_32bit (
  input  [3:0] ALU_Ctrl,
  input  C_in,
  input  [31:0] A,
  input  [31:0] B,
  output [31:0] R,
  output C_out
);

  wire alu_4bit_1_c_out, alu_4bit_2_c_out, alu_4bit_4_c_out, alu_4bit_5_c_out, alu_4bit_6_c_out,
       alu_4bit_7_c_out, alu_4bit_8_c_out;

  ALU_4bit alu_4bit_1 (.ALU_Ctrl(ALU_Ctrl), .C_in(C_in), .A(A[3:0]), .B(B[3:0]), .R(R[3:0]), .C_out(alu_4bit_1_c_out));
  ALU_4bit alu_4bit_2 (
    .ALU_Ctrl(ALU_Ctrl), .C_in(alu_4bit_1_c_out), .A(A[11:8]), .B(B[7:4]), .R(R[7:4]),
    .C_out(alu_4bit_2_c_out));
  ALU_4bit alu_4bit_3 (
    .ALU_Ctrl(ALU_Ctrl), .C_in(alu_4bit_1_c_out), .A(A[11:8]), .B(B[7:4]), .R(R[7:4]),
    .C_out(alu_4bit_2_c_out));
  ALU_4bit alu_4bit_4 (
    .ALU_Ctrl(ALU_Ctrl), .C_in(alu_4bit_2_c_out), .A(A[11:8]), .B(B[11:8]), .R(R[11:8]),
    .C_out(alu_4bit_4_c_out));
  ALU_4bit alu_4bit_5 (
    .ALU_Ctrl(ALU_Ctrl), .C_in(alu_4bit_4_c_out), .A(A[15:12]), .B(B[15:12]), .R(R[15:12]),
    .C_out(alu_4bit_5_c_out));
  ALU_4bit alu_4bit_6 (
    .ALU_Ctrl(ALU_Ctrl), .C_in(alu_4bit_5_c_out), .A(A[19:16]), .B(B[19:16]), .R(R[19:16]),
    .C_out(alu_4bit_6_c_out));
  ALU_4bit alu_4bit_7 (
    .ALU_Ctrl(ALU_Ctrl), .C_in(alu_4bit_6_c_out), .A(A[23:20]), .B(B[23:20]), .R(R[23:20]),
    .C_out(alu_4bit_7_c_out));
  ALU_4bit alu_4bit_8 (
    .ALU_Ctrl(ALU_Ctrl), .C_in(alu_4bit_7_c_out), .A(A[27:24]), .B(B[27:24]), .R(R[27:24]),
    .C_out(alu_4bit_8_c_out));
  ALU_4bit alu_4bit_9 (
    .ALU_Ctrl(ALU_Ctrl), .C_in(alu_4bit_8_c_out), .A(A[31:28]), .B(B[31:28]), .R(R[31:28]), .C_out(C_out));

  assign A[7:4] = A[11:8];
endmodule
