// Logisim project lab4_part2.circ as structural Verilog: 7 circuits, main circuit main
module main (
  input  [31:0] Instruction
);

  wire alu_control_1_alu_src, clock_1_out;
  wire [3:0] alu_control_1_alu_ctrl0;
  wire [31:0] alu_32bit_1_r, bit_extender_1_out, multiplexer_1_out, register_file_1_rdata1,
       register_file_1_rdata2;

  Clock clock_1 (.out(clock_1_out));
  assign bit_extender_1_out = {{20{Instruction[31]}}, Instruction[31:20]};  // Bit_Extender bit_extender_1
  register_file register_file_1 (
    .RReg1(Instruction[19:15]), .RReg2(Instruction[24:20]), .WData(alu_32bit_1_r), .Clock_in(clock_1_out),
    .WReg(Instruction[11:7]), .Write(1'b1), .RData1(register_file_1_rdata1), .RData2(register_file_1_rdata2));
  Multiplexer #(.enable("false"), .width(32)) multiplexer_1 (
    .in0(register_file_1_rdata2), .in1(bit_extender_1_out), .out(multiplexer_1_out),
    .sel(alu_control_1_alu_src));
  ALU_Control alu_control_1 (
    .I30(Instruction[30]), .I14(Instruction[14]), .I13(Instruction[13]), .I12(Instruction[12]),
    .I6(Instruction[6]), .I5(Instruction[5]), .I4(Instruction[4]), .ALU_Ctrl3(alu_control_1_alu_ctrl0[3]),
    .ALU_Ctrl2(alu_control_1_alu_ctrl0[2]), .ALU_Ctrl1(alu_control_1_alu_ctrl0[1]),
    .ALU_Ctrl0(alu_control_1_alu_ctrl0[0]), .ALU_Src(alu_control_1_alu_src));
  ALU_32bit alu_32bit_1 (
    .ALU_Ctrl(alu_control_1_alu_ctrl0), .A(register_file_1_rdata1), .B(multiplexer_1_out), .R(alu_32bit_1_r));  // open: C_in, C_out
endmodule

module FullAdder_1bit (
  input  A,
  input  B,
  input  C_in,
  output S,
  output C_out
);

  wire and_1_out, and_2_out, xor_1_out;

  xor xor_1 (xor_1_out, A, B);
  xor xor_2 (S, xor_1_out, C_in);
  and and_1 (and_1_out, xor_1_out, C_in);
  and and_2 (and_2_out, B, A);
  or or_1 (C_out, and_1_out, and_2_out);
endmodule

module ALU_1bit (
  input  [3:0] ALU_Ctrl,
  input  A,
  input  B,
  input  C_in,
  output R,
  output C_out
);

  wire and_1_out, fulladder_1bit_1_s, multiplexer_1_out, not_1_out, or_1_out, xor_1_out;

  Multiplexer #(.enable("false")) multiplexer_1 (.in0(B), .in1(not_1_out), .out(multiplexer_1_out), .sel(ALU_Ctrl[2]));
  not not_1 (not_1_out, B);
  and and_1 (and_1_out, A, multiplexer_1_out);
  or or_1 (or_1_out, A, multiplexer_1_out);
  xor xor_1 (xor_1_out, A, multiplexer_1_out);
  FullAdder_1bit fulladder_1bit_1 (.A(A), .B(multiplexer_1_out), .C_in(C_in), .S(fulladder_1bit_1_s), .C_out(C_out));
  Multiplexer #(.enable("false"), .select(2)) multiplexer_2 (
    .in0(and_1_out), .in1(or_1_out), .in2(xor_1_out), .in3(fulladder_1bit_1_s), .out(R), .sel(ALU_Ctrl[1:0]));
endmodule

module ALU_Control (
  input  I30,
  input  I14,
  input  I13,
  input  I12,
  input  I6,
  input  I5,
  input  I4,
  output ALU_Ctrl3,
  output ALU_Ctrl2,
  output ALU_Ctrl1,
  output ALU_Ctrl0,
  output ALU_Src
);

  wire and_2_out, not_1_out, not_2_out, not_3_out, not_4_out, not_5_out;

  not not_1 (not_1_out, I14);
  not not_2 (not_2_out, I13);
  not not_3 (not_3_out, I12);
  not not_4 (not_4_out, I5);
  not not_5 (not_5_out, I4);
  and and_1 (ALU_Ctrl2, I30, not_2_out, I5);
  or or_1 (ALU_Ctrl1, not_2_out, not_5_out);
  and and_2 (and_2_out, I13, not_3_out);
  or or_2 (ALU_Src, not_4_out, not_5_out);
  or or_3 (ALU_Ctrl0, not_1_out, and_2_out);

  assign ALU_Ctrl3 = 1'b0;
endmodule

module ALU_4bit (
  input  [3:0] ALU_Ctrl,
  input  C_in,
  input  [3:0] A,
  input  [3:0] B,
  output [3:0] R,
  output C_out
);

  wire alu_1bit_1_c_out, alu_1bit_2_c_out, alu_1bit_3_c_out;

  ALU_1bit alu_1bit_1 (.ALU_Ctrl(ALU_Ctrl), .A(A[0]), .B(B[0]), .C_in(C_in), .R(R[0]), .C_out(alu_1bit_1_c_out));
  ALU_1bit alu_1bit_2 (
    .ALU_Ctrl(ALU_Ctrl), .A(A[1]), .B(B[1]), .C_in(alu_1bit_1_c_out), .R(R[1]), .C_out(alu_1bit_2_c_out));
  ALU_1bit alu_1bit_3 (
    .ALU_Ctrl(ALU_Ctrl), .A(A[2]), .B(B[2]), .C_in(alu_1bit_2_c_out), .R(R[2]), .C_out(alu_1bit_3_c_out));
  ALU_1bit alu_1bit_4 (.ALU_Ctrl(ALU_Ctrl), .A(A[3]), .B(B[3]), .C_in(alu_1bit_3_c_out), .R(R[3]), .C_out(C_out));
endmodule

module ALU_32bit (
  input  [3:0] ALU_Ctrl,
  input  C_in,
  input  [31:0] A,
  input  [31:0] B,
  output [31:0] R,
  output C_out
);

  wire alu_4bit_1_c_out, alu_4bit_2_c_out, alu_4bit_3_c_out, alu_4bit_4_c_out, alu_4bit_5_c_out,
       alu_4bit_6_c_out, alu_4bit_7_c_out;

  ALU_4bit alu_4bit_1 (.ALU_Ctrl(ALU_Ctrl), .C_in(C_in), .A(A[3:0]), .B(B[3:0]), .R(R[3:0]), .C_out(alu_4bit_1_c_out));
  ALU_4bit alu_4bit_2 (
    .ALU_Ctrl(ALU_Ctrl), .C_in(alu_4bit_1_c_out), .A(A[7:4]), .B(B[7:4]), .R(R[7:4]), .C_out(alu_4bit_2_c_out));
  ALU_4bit alu_4bit_3 (
    .ALU_Ctrl(ALU_Ctrl), .C_in(alu_4bit_2_c_out), .A(A[11:8]), .B(B[11:8]), .R(R[11:8]),
    .C_out(alu_4bit_3_c_out));
  ALU_4bit alu_4bit_4 (
    .ALU_Ctrl(ALU_Ctrl), .C_in(alu_4bit_3_c_out), .A(A[15:12]), .B(B[15:12]), .R(R[15:12]),
    .C_out(alu_4bit_4_c_out));
  ALU_4bit alu_4bit_5 (
    .ALU_Ctrl(ALU_Ctrl), .C_in(alu_4bit_4_c_out), .A(A[19:16]), .B(B[19:16]), .R(R[19:16]),
    .C_out(alu_4bit_5_c_out));
  ALU_4bit alu_4bit_6 (
    .ALU_Ctrl(ALU_Ctrl), .C_in(alu_4bit_5_c_out), .A(A[23:20]), .B(B[23:20]), .R(R[23:20]),
    .C_out(alu_4bit_6_c_out));
  ALU_4bit alu_4bit_7 (
    .ALU_Ctrl(ALU_Ctrl), .C_in(alu_4bit_6_c_out), .A(A[27:24]), .B(B[27:24]), .R(R[27:24]),
    .C_out(alu_4bit_7_c_out));
  ALU_4bit alu_4bit_8 (
    .ALU_Ctrl(ALU_Ctrl), .C_in(alu_4bit_7_c_out), .A(A[31:28]), .B(B[31:28]), .R(R[31:28]), .C_out(C_out));
endmodule

module register_file (
  input  [4:0] RReg1,
  input  [4:0] RReg2,
  input  [31:0] WData,
  input  Clock_in,
  input  [4:0] WReg,
  input  Write,
  output [31:0] RData1,
  output [31:0] RData2
);

  wire write1, write2, write3, write4, write5, write6, write7, write8, write9, write10, write11, write12,
       write13, write14, write15, write16, write17, write18, write19, write20, write21, write22, write23,
       write24, write25, write26, write27, write28, write29, write30, write31, write32;
  wire [31:0] Q1, Q2, Q3, Q4, Q5, Q6, Q7, Q8, Q9, Q10, Q11, Q12, Q13, Q14, Q15, Q16, Q17, Q18, Q19, Q20, Q21,
       Q22, Q23, Q24, Q25, Q26, Q27, Q28, Q29, Q30, Q31, Q32;

  Demultiplexer #(.enable("false"), .select(5)) demultiplexer_1 (
    .out0(write1), .out1(write2), .out2(write3), .out3(write4), .out4(write5), .out5(write6), .out6(write7),
    .out7(write8), .out8(write9), .out9(write10), .out10(write11), .out11(write12), .out12(write13),
    .out13(write14), .out14(write15), .out15(write16), .out16(write17), .out17(write18), .out18(write19),
    .out19(write20), .out20(write21), .out21(write22), .out22(write23), .out23(write24), .out24(write25),
    .out25(write26), .out26(write27), .out27(write28), .out28(write29), .out29(write30), .out30(write31),
    .out31(write32), .in(Write), .sel(WReg));
  Register #(.width(32)) register_1 (.D(WData), .en(write1), .clk(Clock_in), .Q(Q1), .clr(Write));
  Register #(.width(32)) register_2 (.D(WData), .en(write3), .clk(Clock_in), .Q(Q3));  // open: clr
  Register #(.width(32)) register_3 (.D(WData), .en(write8), .clk(Clock_in), .Q(Q8));  // open: clr
  Register #(.width(32)) register_4 (.D(WData), .en(write10), .clk(Clock_in), .Q(Q10));  // open: clr
  Register #(.width(32)) register_5 (.D(WData), .en(write12), .clk(Clock_in), .Q(Q12));  // open: clr
  Register #(.width(32)) register_6 (.D(WData), .en(write14), .clk(Clock_in), .Q(Q14));  // open: clr
  Register #(.width(32)) register_7 (.D(WData), .en(write16), .clk(Clock_in), .Q(Q16));  // open: clr
  Register #(.width(32)) register_8 (.D(WData), .en(write18), .clk(Clock_in), .Q(Q18));  // open: clr
  Register #(.width(32)) register_9 (.D(WData), .en(write20), .clk(Clock_in), .Q(Q20));  // open: clr
  Register #(.width(32)) register_10 (.D(WData), .en(write22), .clk(Clock_in), .Q(Q22));  // open: clr
  Register #(.width(32)) register_11 (.D(WData), .en(write24), .clk(Clock_in), .Q(Q24));  // open: clr
  Register #(.width(32)) register_12 (.D(WData), .en(write26), .clk(Clock_in), .Q(Q26));  // open: clr
  Register #(.width(32)) register_13 (.D(WData), .en(write28), .clk(Clock_in), .Q(Q28));  // open: clr
  Register #(.width(32)) register_14 (.D(WData), .en(write30), .clk(Clock_in), .Q(Q30));  // open: clr
  Register #(.width(32)) register_15 (.D(WData), .en(write32), .clk(Clock_in), .Q(Q32));  // open: clr
  Register #(.width(32)) register_16 (.D(WData), .en(write2), .clk(Clock_in), .Q(Q2));  // open: clr
  Register #(.width(32)) register_17 (.D(WData), .en(write4), .clk(Clock_in), .Q(Q4));  // open: clr
  Register #(.width(32)) register_18 (.D(WData), .en(write5), .clk(Clock_in), .Q(Q5));  // open: clr
  Register #(.width(32)) register_19 (.D(WData), .en(write6), .clk(Clock_in), .Q(Q6));  // open: clr
  Register #(.width(32)) register_20 (.D(WData), .en(write7), .clk(Clock_in), .Q(Q7));  // open: clr
  Register #(.width(32)) register_21 (.D(WData), .en(write9), .clk(Clock_in), .Q(Q9));  // open: clr
  Register #(.width(32)) register_22 (.D(WData), .en(write11), .clk(Clock_in), .Q(Q11));  // open: clr
  Register #(.width(32)) register_23 (.D(WData), .en(write13), .clk(Clock_in), .Q(Q13));  // open: clr
  Register #(.width(32)) register_24 (.D(WData), .en(write15), .clk(Clock_in), .Q(Q15));  // open: clr
  Register #(.width(32)) register_25 (.D(WData), .en(write17), .clk(Clock_in), .Q(Q17));  // open: clr
  Register #(.width(32)) register_26 (.D(WData), .en(write19), .clk(Clock_in), .Q(Q19));  // open: clr
  Register #(.width(32)) register_27 (.D(WData), .en(write21), .clk(Clock_in), .Q(Q21));  // open: clr
  Register #(.width(32)) register_28 (.D(WData), .en(write23), .clk(Clock_in), .Q(Q23));  // open: clr
  Register #(.width(32)) register_29 (.D(WData), .en(write25), .clk(Clock_in), .Q(Q25));  // open: clr
  Register #(.width(32)) register_30 (.D(WData), .en(write27), .clk(Clock_in), .Q(Q27));  // open: clr
  Register #(.width(32)) register_31 (.D(WData), .en(write29), .clk(Clock_in), .Q(Q29));  // open: clr
  Register #(.width(32)) register_32 (.D(WData), .en(write31), .clk(Clock_in), .Q(Q31));  // open: clr
  Multiplexer #(.enable("false"), .select(5), .width(32)) multiplexer_1 (
    .in0(Q1), .in1(Q2), .in2(Q3), .in3(Q4), .in4(Q5), .in5(Q6), .in6(Q7), .in7(Q8), .in8(Q9), .in9(Q10),
    .in10(Q11), .in11(Q12), .in12(Q13), .in13(Q14), .in14(Q15), .in15(Q16), .in16(Q17), .in17(Q18),
    .in18(Q19), .in19(Q20), .in20(Q21), .in21(Q22), .in22(Q23), .in23(Q24), .in24(Q25), .in25(Q26),
    .in26(Q27), .in27(Q28), .in28(Q29), .in29(Q30), .in30(Q31), .in31(Q32), .out(RData1), .sel(RReg1));
  Multiplexer #(.enable("false"), .select(5), .width(32)) multiplexer_2 (
    .in0(Q1), .in1(Q2), .in2(Q3), .in3(Q4), .in4(Q5), .in5(Q6), .in6(Q7), .in7(Q8), .in8(Q9), .in9(Q10),
    .in10(Q11), .in11(Q12), .in12(Q13), .in13(Q14), .in14(Q15), .in15(Q16), .in16(Q17), .in17(Q18),
    .in18(Q19), .in19(Q20), .in20(Q21), .in21(Q22), .in22(Q23), .in23(Q24), .in24(Q25), .in25(Q26),
    .in26(Q27), .in27(Q28), .in28(Q29), .in29(Q30), .in30(Q31), .in31(Q32), .out(RData2), .sel(RReg2));
endmodule
